# Fritzing sketch waterer (saved by Fritzing 0.9.3b)
breadboards: 1

parts:
  MCU1 = Raspberry Pi Zero
  VCC1 = Battery block 9V
  S2 = Pushbutton [package="[THT]"]
  R1 = Resistor [tolerance=±5% resistance=1k package=THT]
  Q1 = Basic FET N-Channel [package="DPak [SMD]"]
  L1 = Solenoid
  D1 = Diode [package=diode-1n4001]

nets:
  N1: MCU1.pin_1, MCU1.pin_17, S2.Pin_3, S2.Pin_4
  N2: MCU1.pin_5, S2.Pin_1, S2.Pin_2, R1.Pin_0
  N3: MCU1.pin_6, MCU1.pin_8, MCU1.pin_9, MCU1.pin_14, VCC1.-, Q1.Gate
  N4: VCC1.+, L1.pin2, D1.C
  N5: Q1.source, L1.pin1, D1.A
