# Fritzing sketch air (saved by Fritzing 0.9.3b)
breadboards: 1

parts:
  MCU1 = Raspberry Pi Zero
  DHT1 = DHT22 Humidity and Temperature Sensor

nets:
  N1: MCU1.pin_1, MCU1.pin_17, DHT1.DATA
  N2: MCU1.pin_8, DHT1.NULL
  N3: MCU1.pin_9, MCU1.pin_34, DHT1.VDD
