# Fritzing sketch soil (saved by Fritzing 0.9.3b)
breadboards: 1

parts:
  MCU1 = Raspberry Pi Zero
  ADC1 = MCP3008 [package=dil16]
  Part1 = Soil Moisture Sensor

nets:
  VDD: MCU1.pin_1, MCU1.pin_17, ADC1.VREF, ADC1.VDD, Part1.VCC
  N1: MCU1.pin_9, MCU1.pin_30, ADC1.DGND, ADC1.AGND, Part1.GND
  N2: MCU1.pin_31, ADC1.CLK
  N3: MCU1.pin_33, ADC1.Dout
  N4: MCU1.pin_35, ADC1.Din
  N5: MCU1.pin_37, ADC1.CS/SHDN
  N6: ADC1.CH0, Part1.SIG
